# Fritzing sketch canbus_send_receive (saved by Fritzing 0.9.0b)

parts:
  Part3 = FTDI Basic Programmer
  Receiver = Arduino Pro Mini v13
  Part5 = ElecFreaks Can-Bus Shield
  Sender = Arduino Pro Mini v13
  Part7 = ElecFreaks Can-Bus Shield
  R1 = Resistor [tolerance=±5% resistance=120 package=THT]
  R2 = Resistor [tolerance=±5% resistance=120 package=THT]

nets:
  N1: Part3.DTR, Receiver.DTR
  N2: Part3.RXI, Receiver.D0/TX
  N3: Part3.TXO, Receiver.D1/RX
  VCC: Part3.POWER, Receiver.VCC, Part5.5V, Sender.VCC, Part7.5V
  GND: Part3.GND, Receiver.GND, Part5.GND, Sender.GND, Part7.GND
  N4: Receiver.D13/SCK, Part5.SCK
  N5: Receiver.D12/MISO, Part5.MISO
  N6: Receiver.D11_PWM/MOSI, Part5.MOSI
  N7: Receiver.D10_PWM/SS, Part5.SS
  N8: Receiver.D2, Part5.INT
  N9: Part5.CANH, Part7.CANH, R1.Pin_0, R2.Pin_0
  N10: Part5.CANL, Part7.CANL, R1.Pin_1, R2.Pin_1
  N11: Sender.D13/SCK, Part7.SCK
  N12: Sender.D12/MISO, Part7.MISO
  N13: Sender.D11_PWM/MOSI, Part7.MOSI
  N14: Sender.D10_PWM/SS, Part7.SS
  N15: Sender.D2, Part7.INT

notes:
  Sender
  Receiver

custom parts:
  ElecFreaks Can-Bus Shield: CAN-BUS is a common industrial bus because of its long travel distance, medium communication speed and high reliability. It is commonly found on modern machine tools and as an automotive diagnostic bus. This CAN-BUS Shield adopts MCP2515 CAN Bus controller with SPI interface and MCP2551 CAN transceiver to give your Arduino/Seeeduino CAN-BUS capibility. With an OBD-II converter cable added on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
