# Fritzing sketch canbus_wiring (saved by Fritzing 0.9.0b)

parts:
  Part3 = FTDI Basic Programmer
  Part4 = Arduino Pro Mini v13
  Part5 = ElecFreaks Can-Bus Shield

nets:
  N1: Part3.DTR, Part4.DTR
  N2: Part3.RXI, Part4.D0/TX
  N3: Part3.TXO, Part4.D1/RX
  VCC: Part3.POWER, Part4.VCC, Part5.5V
  GND: Part3.GND, Part4.GND, Part5.GND
  N4: Part4.D13/SCK, Part5.SCK
  N5: Part4.D12/MISO, Part5.MISO
  N6: Part4.D11_PWM/MOSI, Part5.MOSI
  N7: Part4.D10_PWM/SS, Part5.SS
  N8: Part4.D2, Part5.INT

custom parts:
  ElecFreaks Can-Bus Shield: CAN-BUS is a common industrial bus because of its long travel distance, medium communication speed and high reliability. It is commonly found on modern machine tools and as an automotive diagnostic bus. This CAN-BUS Shield adopts MCP2515 CAN Bus controller with SPI interface and MCP2551 CAN transceiver to give your Arduino/Seeeduino CAN-BUS capibility. With an OBD-II converter cable added on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
